// Logisim project exer_1.circ as structural Verilog: 6 circuits, main circuit main
module main (
  input  in_1,
  input  in_2,
  input  in_3,
  input  in_4,
  input  in_5,
  input  in_6,
  input  in_7,
  input  in_8,
  input  in_9,
  input  a,
  input  s0,
  input  b,
  input  s1,
  input  c,
  input  d,
  output out_16,
  output out_17,
  output out_18,
  output out_19,
  output out_20
);

  NAND nand_1 (.a(in_1), .b(in_2), .out_3(out_16));
  NOR nor_1 (.a(in_3), .b(in_4), .out_3(out_17));
  XOR xor_1 (.a(in_5), .b(in_6), .out_3(out_18));
  _2_1MUX u_2_1mux_1 (.a(in_7), .s(in_8), .b(in_9), .out_4(out_19));
  _4_1MUX u_4_1mux_1 (.a(a), .s0(s0), .b(b), .s1(s1), .c(c), .d(d), .out_7(out_20));
endmodule

module NAND (
  input  a,
  input  b,
  output out_3
);

  wire and_1_out;

  and and_1 (and_1_out, a, b);
  not not_1 (out_3, and_1_out);
endmodule

module NOR (
  input  a,
  input  b,
  output out_3
);

  wire or_1_out;

  or or_1 (or_1_out, a, b);
  not not_1 (out_3, or_1_out);
endmodule

module XOR (
  input  a,
  input  b,
  output out_3
);

  wire and_1_out, and_2_out, not_1_out, not_2_out;

  not not_1 (not_1_out, b);
  not not_2 (not_2_out, a);
  and and_1 (and_1_out, a, not_1_out);
  and and_2 (and_2_out, not_2_out, b);
  or or_1 (out_3, and_1_out, and_2_out);
endmodule

module _2_1MUX (
  input  a,
  input  s,
  input  b,
  output out_4
);

  wire and_1_out, and_2_out, not_1_out;

  not not_1 (not_1_out, s);
  and and_1 (and_1_out, not_1_out, a);
  and and_2 (and_2_out, s, b);
  or or_1 (out_4, and_1_out, and_2_out);
endmodule

module _4_1MUX (
  input  a,
  input  s0,
  input  b,
  input  s1,
  input  c,
  input  d,
  output out_7
);

  wire and_1_out, and_2_out, and_3_out, and_4_out, and_5_out, and_6_out, not_1_out, not_2_out, not_3_out,
       or_1_out, or_2_out;

  not not_1 (not_1_out, s0);
  not not_2 (not_2_out, s0);
  and and_1 (and_1_out, not_1_out, a);
  and and_2 (and_2_out, s0, b);
  and and_3 (and_3_out, not_2_out, c);
  and and_4 (and_4_out, s0, d);
  or or_1 (or_1_out, and_1_out, and_2_out);
  or or_2 (or_2_out, and_3_out, and_4_out);
  not not_3 (not_3_out, s1);
  and and_5 (and_5_out, or_1_out, not_3_out);
  and and_6 (and_6_out, s1, or_2_out);
  or or_3 (out_7, and_5_out, and_6_out);
endmodule
