// Logisim project Ex1.circ as structural Verilog
module Ex1 (
  input  [7:0] _8_bit_inp,
  output Out1,
  output [7:0] Out2
);

  and and_1 (Out1, _8_bit_inp[0], _8_bit_inp[7]);
  not not_1 (Out2[7], _8_bit_inp[7]);

  assign Out2[6:0] = _8_bit_inp[6:0];
endmodule
