// Logisim project Ex2.circ as structural Verilog: 5 circuits, main circuit main
module main (
  input  [15:0] in_1,
  input  [3:0] in_2,
  output [15:0] out_3
);

  wire [15:0] sub0_1_out_3, sub1_1_out_3, sub2_1_out_3;

  sub0 sub0_1 (.in_1(in_2[0]), .in_2(in_1), .out_3(sub0_1_out_3));
  sub1 sub1_1 (.in_1(in_2[1]), .in_2(sub0_1_out_3), .out_3(sub1_1_out_3));
  sub2 sub2_1 (.in_1(in_2[2]), .in_2(sub1_1_out_3), .out_3(sub2_1_out_3));
  sub3 sub3_1 (.in_1(in_2[3]), .in_2(sub2_1_out_3), .out_3(out_3));

  // Other names for the same wires on the sheet: _0 = in_2[0]; _1 = in_2[1]; _2 = in_2[2]; _3 = in_2[3]
endmodule

module sub0 (
  input  in_1,
  input  [15:0] in_2,
  output [15:0] out_3
);

  Multiplexer #(.width(16)) multiplexer_1 (
    .in0(in_2), .in1({in_2[0], in_2[15:1]}), .out(out_3), .sel(in_1));  // open: en
endmodule

module sub1 (
  input  in_1,
  input  [15:0] in_2,
  output [15:0] out_3
);

  Multiplexer #(.width(16)) multiplexer_1 (
    .in0(in_2), .in1({in_2[1:0], in_2[15:2]}), .out(out_3), .sel(in_1));  // open: en
endmodule

module sub2 (
  input  in_1,
  input  [15:0] in_2,
  output [15:0] out_3
);

  Multiplexer #(.width(16)) multiplexer_1 (
    .in0(in_2), .in1({in_2[3:0], in_2[15:4]}), .out(out_3), .sel(in_1));  // open: en
endmodule

module sub3 (
  input  in_1,
  input  [15:0] in_2,
  output [15:0] out_3
);

  Multiplexer #(.width(16)) multiplexer_1 (
    .in0(in_2), .in1({in_2[7:0], in_2[15:8]}), .out(out_3), .sel(in_1));  // open: en
endmodule
