// Logisim project lab5ALU.circ as structural Verilog: 9 circuits, main circuit ALU
// LAB12-ALU
module ALU (
  input  [31:0] ALU_Source_1,
  input  [31:0] ALU_Source_2,
  input  [2:0] ALU_Control,
  output [31:0] ALU_Result
);

  wire [4:0] bit_extender_1_out;
  wire [31:0] \and , exclusive_or, inclusive_or, rotate_left, rotate_right, sll, sra, srl;

  // Probe on ALU_Source_1
  // Probe on ALU_Source_2
  Bit_Extender #(.in_width(32), .out_width(5)) bit_extender_1 (.in(ALU_Source_2), .out(bit_extender_1_out));
  Inclusive_Or inclusive_or_1 (.in_1(ALU_Source_1), .in_2(ALU_Source_2), .out_3(inclusive_or));
  AND u_And (.in_1(ALU_Source_1), .in_2(ALU_Source_2), .out_3(\and ));
  Exclusive_Or exclusive_or_1 (.in_1(ALU_Source_1), .in_2(ALU_Source_2), .out_3(exclusive_or));
  SLL sll_1 (.in_1(ALU_Source_1), .in_2(bit_extender_1_out), .out_3(sll));
  SRL srl_1 (.in_1(ALU_Source_1), .in_2(bit_extender_1_out), .out_3(srl));
  SRA sra_1 (.in_1(ALU_Source_1), .in_2(bit_extender_1_out), .out_3(sra));
  Rotate_Right rotate_right_1 (.in_1(ALU_Source_1), .in_2(bit_extender_1_out), .out_3(rotate_right));
  Rotate_Left rotate_left_1 (.in_1(ALU_Source_1), .in_2(bit_extender_1_out), .out_3(rotate_left));
  // Probe on ALU_Result
  Multiplexer #(.select(3), .width(32)) multiplexer_1 (
    .in0(inclusive_or), .in1(\and ), .in2(exclusive_or), .in3(sll), .in4(srl), .in5(sra), .in6(rotate_right),
    .in7(rotate_left), .sel(ALU_Control));  // open: out, en

  // Other names for the same wires on the sheet: control[2:0] = ALU_Control; result[31:0] = ALU_Result;
  //   source1[31:0] = ALU_Source_1; source2[31:0] = ALU_Source_2

  // Notes on the sheet:
  //   DO NOT CROSS WIRES
  //   OVER THIS BOX
  //   DO NOT CROSS WIRES
  //   OVER THIS BOX
  //   COMPUTE ALL POSSIBLE OPERATIONS
  //   DO NOT CROSS WIRES
  //   OVER THIS BOX
  //   SELECT THE REQUESTED RESULT
endmodule

module Inclusive_Or (
  input  [31:0] in_1,
  input  [31:0] in_2,
  output [31:0] out_3
);

  assign out_3 = in_1 | in_2;  // OR_Gate or_1, 32 bits wide
endmodule

module AND (
  input  [31:0] in_1,
  input  [31:0] in_2,
  output [31:0] out_3
);

  assign out_3 = in_1 & in_2;  // AND_Gate and_1, 32 bits wide
endmodule

module Exclusive_Or (
  input  [31:0] in_1,
  input  [31:0] in_2,
  output [31:0] out_3
);

  wire [31:0] and_1_out, and_2_out, not_1_out, not_2_out;

  assign not_1_out = ~in_2;  // NOT_Gate not_1, 32 bits wide
  assign not_2_out = ~in_1;  // NOT_Gate not_2, 32 bits wide
  assign and_1_out = in_1 & not_1_out;  // AND_Gate and_1, 32 bits wide
  assign and_2_out = not_2_out & in_2;  // AND_Gate and_2, 32 bits wide
  assign out_3 = and_2_out | and_1_out;  // OR_Gate or_1, 32 bits wide
endmodule

module SLL (
  input  [31:0] in_1,
  input  [4:0] in_2,
  output [31:0] out_3
);

  Shifter #(.width(32)) shifter_1 (.in(in_1), .\dist (in_2), .out(out_3));
endmodule

module SRL (
  input  [31:0] in_1,
  input  [4:0] in_2,
  output [31:0] out_3
);

  Shifter #(.width(32), .shift("lr")) shifter_1 (.in(in_1), .\dist (in_2), .out(out_3));
endmodule

module SRA (
  input  [31:0] in_1,
  input  [4:0] in_2,
  output [31:0] out_3
);

  Shifter #(.width(32), .shift("ar")) shifter_1 (.in(in_1), .\dist (in_2), .out(out_3));
endmodule

module Rotate_Right (
  input  [31:0] in_1,
  input  [4:0] in_2,
  output [31:0] out_3
);

  wire [4:0] subtractor_1_out;
  wire [31:0] sll_1_out_3, srl_1_out_3;

  SRL srl_1 (.in_1(in_1), .in_2(in_2), .out_3(srl_1_out_3));
  Subtractor #(.width(5)) subtractor_1 (.a({5{1'b0}}), .b(in_2), .out(subtractor_1_out));  // open: bin, bout
  SLL sll_1 (.in_1(in_1), .in_2(subtractor_1_out), .out_3(sll_1_out_3));
  assign out_3 = srl_1_out_3 | sll_1_out_3;  // OR_Gate or_1, 32 bits wide
endmodule

module Rotate_Left (
  input  [31:0] in_1,
  input  [4:0] in_2,
  output [31:0] out_3
);

  wire [4:0] subtractor_1_out;
  wire [31:0] sll_1_out_3, srl_1_out_3;

  SLL sll_1 (.in_1(in_1), .in_2(in_2), .out_3(sll_1_out_3));
  Subtractor #(.width(5)) subtractor_1 (.a({5{1'b0}}), .b(in_2), .out(subtractor_1_out));  // open: bin, bout
  SRL srl_1 (.in_1(in_1), .in_2(subtractor_1_out), .out_3(srl_1_out_3));
  assign out_3 = sll_1_out_3 | srl_1_out_3;  // OR_Gate or_1, 32 bits wide
endmodule
