// Logisim project cpu.circ as structural Verilog: 2 circuits, main circuit main
module main (
  input  [15:0] INSTRUCTION,
  input  CLOCK,
  output [15:0] FETCH_ADDRESS,
  output [15:0] s0_Value,
  output [15:0] s1_Value,
  output [15:0] s2_Value,
  output [15:0] ra_Value,
  output [15:0] sp_Value,
  output [15:0] HI_Value,
  output [15:0] LO_Value
);

  wire ALUsrc, bne, branch, check_branch, comparator_1_eq, comparator_2_eq, comparator_3_eq, comparator_4_eq,
       comparator_5_eq, comparator_6_eq, Ext_Op, j, j_and_jr, main_2_equal, MemToReg, MemWR,
       multiplexer_5_out, multiply, not_1_out, or_1_out, or_2_out, R, RegWR, U;
  wire [1:0] adder_4_out, adder_5_out, bit_extender_5_out, bit_extender_6_out, bit_extender_7_out,
       bit_extender_8_out, shifter_2_out, shifter_3_out, write_src;
  wire [2:0] ALUctr, extend_rd, inp2, WR_reg;
  wire [15:0] adder_2_out, ALU_out, and_1_out, bit_extender_1_out, bit_extender_2_out, bit_extender_3_out,
       bit_extender_4_out, bubble_instr, immediate_pc, jump_addr, main_1_read_data_1, main_1_read_data_2,
       main_2_result_2, MEM_p5, multiplexer_6_out, multiplexer_7_out, multiplexer_8_out, multiplexer_9_out,
       multiplexer_10_out, multiplexer_11_out, multiplexer_12_out, PC_plus_2, shifter_1_out,
       subtractor_1_out, toBranch;

  assign bit_extender_1_out = {{10{1'b0}}, bubble_instr[5:0]};  // Bit_Extender bit_extender_1
  assign bit_extender_2_out = {{10{bubble_instr[5]}}, bubble_instr[5:0]};  // Bit_Extender bit_extender_2
  Multiplexer #(.width(3), .enable("false")) multiplexer_1 (
    .in0(bubble_instr[5:3]), .in1(bubble_instr[11:9]), .out(inp2), .sel(or_1_out));
  or or_1 (or_1_out, MemWR, branch);
  Multiplexer #(.width(3), .enable("false")) multiplexer_2 (
    .in0(bubble_instr[11:9]), .in1(extend_rd), .out(WR_reg), .sel(U));
  Multiplexer #(.width(16), .enable("false")) multiplexer_3 (
    .in0(bit_extender_1_out), .in1(bit_extender_2_out), .out(immediate_pc), .sel(Ext_Op));
  assign and_1_out = 16'hfc00 & FETCH_ADDRESS;  // AND_Gate and_1, 16 bits wide
  Subtractor #(.width(16)) subtractor_1 (.a(FETCH_ADDRESS), .b(16'h2), .out(subtractor_1_out));  // open: bin, bout
  assign bit_extender_3_out = {{6{1'b0}}, bubble_instr[9:0]};  // Bit_Extender bit_extender_3
  Adder #(.width(16)) adder_1 (.a(and_1_out), .b(bit_extender_3_out), .out(jump_addr));  // open: cin, cout
  Adder #(.width(16)) adder_2 (.a(immediate_pc), .b(subtractor_1_out), .out(adder_2_out));  // open: cin, cout
  Multiplexer #(.width(16), .enable("false")) multiplexer_4 (
    .in0(PC_plus_2), .in1(adder_2_out), .out(toBranch), .sel(check_branch));
  and and_2 (check_branch, multiplexer_5_out, branch);
  regfile_main main_1 (
    .Read_Register_1(bubble_instr[8:6]), .Read_Register_2(inp2), .Write_Register(WR_reg),
    .Write_Data(multiplexer_7_out), .Write_Enable(RegWR), .Clock(CLOCK), .Read_Data_1(main_1_read_data_1),
    .Read_Data_2(main_1_read_data_2), .s0_Value(s0_Value), .s1_Value(s1_Value), .s2_Value(s2_Value),
    .ra_Value(ra_Value), .sp_Value(sp_Value));
  Multiplexer #(.enable("false")) multiplexer_5 (
    .in0(main_2_equal), .in1(not_1_out), .out(multiplexer_5_out), .sel(bne));
  Multiplexer #(.width(16), .enable("false")) multiplexer_6 (
    .in0(main_1_read_data_2), .in1(immediate_pc), .out(multiplexer_6_out), .sel(ALUsrc));
  not not_1 (not_1_out, main_2_equal);
  alu_main main_2 (
    .Switch(ALUctr), .X(main_1_read_data_1), .Equal(main_2_equal), .Result(ALU_out), .Y(multiplexer_6_out),
    .Result_2(main_2_result_2));  // open: out_7, out_8
  Multiplexer #(.select(2), .width(16), .enable("false")) multiplexer_7 (
    .in0(multiplexer_10_out), .in1(LO_Value), .in2(HI_Value), .in3(FETCH_ADDRESS), .out(multiplexer_7_out),
    .sel(write_src));
  Multiplexer #(.width(16), .enable("false")) multiplexer_8 (
    .in0(ALU_out), .in1(jump_addr), .out(multiplexer_8_out), .sel(j));
  Multiplexer #(.width(16), .enable("false")) multiplexer_9 (
    .in0(toBranch), .in1(multiplexer_8_out), .out(multiplexer_9_out), .sel(j_and_jr));
  Register #(.width(16)) PC (.D(multiplexer_9_out), .Q(FETCH_ADDRESS), .clk(CLOCK));  // open: en, clr
  Register #(.width(16)) HI (.D(main_2_result_2), .en(multiply), .Q(HI_Value), .clk(CLOCK));  // open: clr
  assign bit_extender_4_out = {{6{1'b0}}, bubble_instr[9:0]};  // Bit_Extender bit_extender_4
  assign bit_extender_5_out = {{1{1'b0}}, multiply};  // Bit_Extender bit_extender_5
  Comparator #(.width(4), .mode("unsigned")) comparator_1 (
    .a(bubble_instr[15:12]), .b(4'b0001), .eq(comparator_1_eq));  // open: gt, lt
  // mem_main MEM: pin names not known; wires that end beside it: ALU_out, main_1_read_data_2, MemWR, CLOCK, MEM_p5
  Adder #(.width(16)) adder_3 (.a(FETCH_ADDRESS), .b(16'h2), .out(PC_plus_2));  // open: cin, cout
  Shifter #(.width(16)) shifter_1 (.in(bit_extender_4_out), .\dist (4'b0110), .out(shifter_1_out));
  assign bit_extender_6_out = {{1{1'b0}}, comparator_1_eq};  // Bit_Extender bit_extender_6
  Shifter #(.width(2)) shifter_2 (.in(bit_extender_5_out), .\dist (1'b1), .out(shifter_2_out));
  Multiplexer #(.width(16), .enable("false")) multiplexer_10 (
    .in0(ALU_out), .in1(MEM_p5), .out(multiplexer_10_out), .sel(MemToReg));
  Adder #(.width(2)) adder_4 (.a(bit_extender_6_out), .b(shifter_2_out), .out(adder_4_out));  // open: cin, cout
  Multiplexer #(.select(2), .width(16), .enable("false")) multiplexer_11 (
    .in0(LO_Value), .in1(shifter_1_out), .in2(ALU_out), .out(multiplexer_11_out), .sel(adder_4_out));  // open: in3
  Comparator #(.width(3), .mode("unsigned")) comparator_2 (
    .a(bubble_instr[2:0]), .b(3'b111), .eq(comparator_2_eq));  // open: gt, lt
  Register #(.width(16)) LO (.D(multiplexer_11_out), .Q(LO_Value), .clk(CLOCK));  // open: en, clr
  and and_3 (multiply, R, comparator_2_eq);
  Comparator #(.width(4), .mode("unsigned")) comparator_3 (
    .a(bubble_instr[15:12]), .b(4'b1101), .eq(comparator_3_eq));  // open: gt, lt
  Comparator #(.width(4), .mode("unsigned")) comparator_4 (
    .a(bubble_instr[15:12]), .b(4'b1100), .eq(comparator_4_eq));  // open: gt, lt
  assign bit_extender_7_out = {{1{1'b0}}, comparator_3_eq};  // Bit_Extender bit_extender_7
  assign bit_extender_8_out = {{1{1'b0}}, comparator_4_eq};  // Bit_Extender bit_extender_8
  Comparator #(.width(4), .mode("unsigned")) comparator_5 (
    .a(bubble_instr[15:12]), .b(4'b0010), .eq(comparator_5_eq));  // open: gt, lt
  Comparator #(.width(4), .mode("unsigned")) comparator_6 (
    .a(bubble_instr[15:12]), .b(4'b0011), .eq(comparator_6_eq));  // open: gt, lt
  or or_2 (or_2_out, check_branch, j_and_jr);
  Shifter #(.width(2)) shifter_3 (.in(bit_extender_8_out), .\dist (1'b1), .out(shifter_3_out));
  Multiplexer #(.width(16), .enable("false")) multiplexer_12 (
    .in0(INSTRUCTION), .in1({16{1'b0}}), .out(multiplexer_12_out), .sel(or_2_out));
  Adder #(.width(2)) adder_5 (.a(bit_extender_7_out), .b(shifter_3_out), .out(adder_5_out));  // open: cin, cout
  or or_3 (j_and_jr, comparator_5_eq, comparator_6_eq);
  ControlUnit controlunit_1 (
    .opcode(bubble_instr[15:12]), .funct(bubble_instr[2:0]), .branch(branch), .Jump(j), .Ext_Op(Ext_Op),
    .ALUsrc(ALUsrc), .MemToReg(MemToReg), .MemWri(MemWR), .R_type(R), .RegWri(RegWR), .ALUctr(ALUctr),
    .Utype(U), .branch_ne(bne));
  Register #(.width(16)) pipe_register (.D(multiplexer_12_out), .Q(bubble_instr), .clk(CLOCK));  // open: en, clr
  Multiplexer #(.width(2), .enable("false")) multiplexer_13 (
    .in0(adder_5_out), .in1(2'b11), .out(write_src), .sel(j_and_jr));
  assign extend_rd = {{1{1'b0}}, bubble_instr[11:10]};  // Bit_Extender bit_extender_9

  // Other names for the same wires on the sheet: extend_immediate[9:0] = bubble_instr[9:0];
  //   funct[2:0] = bubble_instr[2:0]; immediate[5:0] = bubble_instr[5:0]; rt[2:0] = bubble_instr[5:3];
  //   rs[2:0] = bubble_instr[8:6]; rd[2:0] = bubble_instr[11:9]; opcode[3:0] = bubble_instr[15:12]; clk = CLOCK;
  //   fetch_addr[15:0] = FETCH_ADDRESS; PC[15:0] = FETCH_ADDRESS; HI[15:0] = HI_Value; LO[15:0] = LO_Value;
  //   ra[15:0] = ra_Value; s0[15:0] = s0_Value; s1[15:0] = s1_Value; s2[15:0] = s2_Value; sp[15:0] = sp_Value

  // Notes on the sheet:
  //   Output
  //   Determine inp rd
  //   Determine inp rt
  //   PC Immediate
  //   These are outputs/inputs from run.circ
  //   Inputs
  //   Jump Address
  //   These are DEBUG/TEST outputs from your circuit.
  //   PC + 2
  //   Multiply
  //   Check if it's instr/bubble
  //   Control Module
  //   Decode Module
endmodule

module ControlUnit (
  input  [3:0] opcode,
  input  [2:0] funct,
  output branch,
  output Jump,
  output Ext_Op,
  output ALUsrc,
  output MemToReg,
  output MemWri,
  output R_type,
  output RegWri,
  output [2:0] ALUctr,
  output Utype,
  output branch_ne
);

  wire and_2_out, comparator_1_eq, comparator_2_eq, comparator_3_eq, comparator_4_eq, comparator_5_eq,
       comparator_6_eq, comparator_7_eq, comparator_8_eq, comparator_9_eq, comparator_10_eq,
       comparator_13_eq, comparator_14_eq, comparator_15_eq, comparator_18_eq, comparator_19_eq,
       comparator_20_eq, comparator_21_eq, comparator_22_eq, comparator_23_eq, not_1_out, not_2_out,
       not_3_out, or_4_out;
  wire [2:0] multiplexer_1_out;

  Comparator #(.width(4), .mode("unsigned")) comparator_1 (
    .a(opcode), .b(4'b0011), .eq(comparator_1_eq));  // open: gt, lt
  Comparator #(.width(4), .mode("unsigned")) comparator_2 (
    .a(opcode), .b(4'b0100), .eq(comparator_2_eq));  // open: gt, lt
  Comparator #(.width(4), .mode("unsigned")) comparator_3 (
    .a(opcode), .b(4'b0101), .eq(comparator_3_eq));  // open: gt, lt
  Comparator #(.width(4), .mode("unsigned")) comparator_4 (
    .a(opcode), .b(4'b0110), .eq(comparator_4_eq));  // open: gt, lt
  Comparator #(.width(4), .mode("unsigned")) comparator_5 (
    .a(opcode), .b(4'b0111), .eq(comparator_5_eq));  // open: gt, lt
  Comparator #(.width(4), .mode("unsigned")) comparator_6 (
    .a(opcode), .b(4'b1010), .eq(comparator_6_eq));  // open: gt, lt
  Comparator #(.width(4), .mode("unsigned")) comparator_7 (
    .a(opcode), .b(4'b1011), .eq(comparator_7_eq));  // open: gt, lt
  Comparator #(.width(4), .mode("unsigned")) comparator_8 (
    .a(opcode), .b(4'b0001), .eq(comparator_8_eq));  // open: gt, lt
  Comparator #(.width(4), .mode("unsigned")) comparator_9 (
    .a(opcode), .b(4'b0010), .eq(comparator_9_eq));  // open: gt, lt
  Comparator #(.width(4), .mode("unsigned")) comparator_10 (
    .a(opcode), .b(4'b0100), .eq(comparator_10_eq));  // open: gt, lt
  Comparator #(.width(4), .mode("unsigned")) comparator_11 (.a(opcode), .b(4'b0010), .eq(Jump));  // open: gt, lt
  Comparator #(.width(4), .mode("unsigned")) comparator_12 (.a(opcode), .b(4'b0101), .eq(branch_ne));  // open: gt, lt
  or or_1 (Ext_Op, comparator_1_eq, comparator_2_eq, comparator_3_eq, comparator_4_eq, comparator_5_eq, comparator_6_eq, comparator_7_eq);
  or or_2 (branch, comparator_10_eq, branch_ne);
  or or_3 (Utype, comparator_8_eq, comparator_9_eq);
  Comparator #(.width(4), .mode("unsigned")) comparator_13 (
    .a(opcode), .b(4'b0000), .eq(comparator_13_eq));  // open: gt, lt
  not not_1 (not_1_out, comparator_13_eq);
  not not_2 (not_2_out, comparator_14_eq);
  Comparator #(.width(4), .mode("unsigned")) comparator_14 (
    .a(opcode), .b(4'b0100), .eq(comparator_14_eq));  // open: gt, lt
  Comparator #(.width(4), .mode("unsigned")) comparator_15 (
    .a(opcode), .b(4'b0101), .eq(comparator_15_eq));  // open: gt, lt
  not not_3 (not_3_out, comparator_15_eq);
  Comparator #(.width(4), .mode("unsigned")) comparator_16 (.a(opcode), .b(4'b1010), .eq(MemToReg));  // open: gt, lt
  Comparator #(.width(4), .mode("unsigned")) comparator_17 (.a(opcode), .b(4'b0000), .eq(R_type));  // open: gt, lt
  Multiplexer #(.select(4), .width(3), .enable("false")) multiplexer_1 (
    .in3(3'b010), .in4(3'b010), .in5(3'b010), .in6(3'b010), .in7(3'b110), .in8(3'b011), .in9(3'b100),
    .in10(3'b010), .in11(3'b010), .out(multiplexer_1_out), .sel(opcode));  // open: in0, in1, in2, in12, in13, in14, in15
  Comparator #(.width(4), .mode("unsigned")) comparator_18 (
    .a(opcode), .b(4'b0000), .eq(comparator_18_eq));  // open: gt, lt
  Comparator #(.width(3), .mode("unsigned")) comparator_19 (
    .a(funct), .b(3'b111), .eq(comparator_19_eq));  // open: gt, lt
  Comparator #(.width(4), .mode("unsigned")) comparator_20 (
    .a(opcode), .b(4'b0001), .eq(comparator_20_eq));  // open: gt, lt
  Comparator #(.width(4), .mode("unsigned")) comparator_21 (
    .a(opcode), .b(4'b0100), .eq(comparator_21_eq));  // open: gt, lt
  Comparator #(.width(4), .mode("unsigned")) comparator_22 (
    .a(opcode), .b(4'b0101), .eq(comparator_22_eq));  // open: gt, lt
  Comparator #(.width(4), .mode("unsigned")) comparator_23 (
    .a(opcode), .b(4'b1011), .eq(comparator_23_eq));  // open: gt, lt
  and and_1 (ALUsrc, not_1_out, not_2_out, not_3_out);
  Multiplexer #(.width(3), .enable("false")) multiplexer_2 (
    .in0(multiplexer_1_out), .in1(funct), .out(ALUctr), .sel(R_type));
  and and_2 (and_2_out, comparator_18_eq, comparator_19_eq);
  not not_4 (RegWri, or_4_out);
  or or_4 (or_4_out, and_2_out, comparator_20_eq, comparator_21_eq, comparator_22_eq, comparator_23_eq);
  Comparator #(.width(4), .mode("unsigned")) comparator_24 (.a(opcode), .b(4'b1011), .eq(MemWri));  // open: gt, lt

  // Other names for the same wires on the sheet: bne = branch_ne; MemWR = MemWri; R = R_type; RegWR = RegWri;
  //   U = Utype

  // Notes on the sheet:
  //   Input
  //   Output: Control Signal
  //   Extend Opcode
  //   U Type
  //   Branch
  //   jump
  //   bne
  //   ALU Source
  //   Memory to Register
  //   R tyoe
  //   ALU Control
  //   Memory Write
endmodule
