// Logisim project regfile.circ as structural Verilog: 1 circuit, main circuit main
module main (
  input  [2:0] Read_Register_1,
  input  [2:0] Read_Register_2,
  input  [2:0] Write_Register,
  input  [15:0] Write_Data,
  input  Write_Enable,
  input  Clock,
  output [15:0] s0_Value,
  output [15:0] s1_Value,
  output [15:0] s2_Value,
  output [15:0] ra_Value,
  output [15:0] sp_Value,
  output [15:0] Read_Data_1,
  output [15:0] Read_Data_2
);

  wire demultiplexer_1_out1, demultiplexer_1_out2, demultiplexer_1_out3, demultiplexer_1_out4,
       demultiplexer_1_out5, demultiplexer_1_out6, demultiplexer_1_out7;
  wire [15:0] _00, _05, _06;

  Demultiplexer #(.select(3), .enable("false")) demultiplexer_1 (
    .out1(demultiplexer_1_out1), .out2(demultiplexer_1_out2), .out3(demultiplexer_1_out3),
    .out4(demultiplexer_1_out4), .out5(demultiplexer_1_out5), .out6(demultiplexer_1_out6),
    .out7(demultiplexer_1_out7), .in(Write_Enable), .sel(Write_Register));  // open: out0
  Multiplexer #(.select(3), .width(16), .enable("false")) multiplexer_1 (
    .in0(_00), .in1(ra_Value), .in2(s0_Value), .in3(s1_Value), .in4(s2_Value), .in5(_05), .in6(_06),
    .in7(sp_Value), .out(Read_Data_1), .sel(Read_Register_1));
  Multiplexer #(.select(3), .width(16), .enable("false")) multiplexer_2 (
    .in0(_00), .in1(ra_Value), .in2(s0_Value), .in3(s1_Value), .in4(s2_Value), .in5(_05), .in6(_06),
    .in7(sp_Value), .out(Read_Data_2), .sel(Read_Register_2));
  Register #(.width(16)) register_1 (.Q(_00), .clk(Clock));  // open: D, en, clr
  Register #(.width(16)) register_2 (
    .D(Write_Data), .en(demultiplexer_1_out1), .Q(ra_Value), .clk(Clock));  // open: clr
  Register #(.width(16)) register_3 (
    .D(Write_Data), .en(demultiplexer_1_out2), .Q(s0_Value), .clk(Clock));  // open: clr
  Register #(.width(16)) register_4 (
    .D(Write_Data), .en(demultiplexer_1_out3), .Q(s1_Value), .clk(Clock));  // open: clr
  Register #(.width(16)) register_5 (
    .D(Write_Data), .en(demultiplexer_1_out4), .Q(s2_Value), .clk(Clock));  // open: clr
  Register #(.width(16)) register_6 (.D(Write_Data), .en(demultiplexer_1_out5), .Q(_05), .clk(Clock));  // open: clr
  Register #(.width(16)) register_7 (.D(Write_Data), .en(demultiplexer_1_out6), .Q(_06), .clk(Clock));  // open: clr
  Register #(.width(16)) register_8 (
    .D(Write_Data), .en(demultiplexer_1_out7), .Q(sp_Value), .clk(Clock));  // open: clr

  // Other names for the same wires on the sheet: _01[15:0] = ra_Value; _02[15:0] = s0_Value; _03[15:0] = s1_Value;
  //   _04[15:0] = s2_Value; _07[15:0] = sp_Value; clk = Clock; read_data1[15:0] = Read_Data_1;
  //   read_data2[15:0] = Read_Data_2; read_reg1[2:0] = Read_Register_1; read_reg2[2:0] = Read_Register_2;
  //   write_en = Write_Enable; write_reg[2:0] = Write_Register

  // Notes on the sheet:
  //   INPUTS to your circuit
  //   DON'T CHANGE THE LOCATIONS OF THE INPUTS AND OUTPUTS!
  //   These are DEBUG/TEST outputs from your circuit.
  //   OUTPUTS from your circuit
endmodule
