// Logisim project alu.circ as structural Verilog: 1 circuit, main circuit main
module main (
  input  [15:0] X,
  input  [15:0] Y,
  input  [2:0] Switch,
  output Equal,
  output [15:0] Result,
  output [15:0] Result_2,
  output [15:0] out_7,
  output [15:0] out_8
);

  wire comparator_2_lt;
  wire [3:0] bit_extender_1_out, bit_extender_2_out;
  wire [15:0] add, \and , \or , sll, slt, srl, \xor ;

  Multiplexer #(.select(3), .width(16)) multiplexer_1 (
    .in0(sll), .in1(srl), .in2(add), .in3(\and ), .in4(\or ), .in5(\xor ), .in6(slt), .in7(out_7),
    .out(Result), .sel(Switch));  // open: en
  Comparator #(.width(16)) comparator_1 (.a(X), .b(Y), .eq(Equal));  // open: gt, lt
  Bit_Extender #(.in_width(16), .out_width(4)) bit_extender_1 (.in(Y), .out(bit_extender_1_out));
  Bit_Extender #(.in_width(16), .out_width(4)) bit_extender_2 (.in(Y), .out(bit_extender_2_out));
  Adder #(.width(16)) adder_1 (.a(X), .b(Y), .out(add));  // open: cin, cout
  assign \and  = X & Y;  // AND_Gate and_1, 16 bits wide
  assign \or  = X | Y;  // OR_Gate or_1, 16 bits wide
  assign \xor  = X ^ Y;  // XOR_Gate xor_1, 16 bits wide
  Comparator #(.width(16)) comparator_2 (.a(X), .b(Y), .lt(comparator_2_lt));  // open: gt, eq
  assign slt = {{15{1'b0}}, comparator_2_lt};  // Bit_Extender bit_extender_3
  Multiplier #(.width(16)) multiplier_1 (.a(X), .b(Y), .out(out_7), .cout(out_8));  // open: cin
  Shifter #(.width(16)) shifter_1 (.in(X), .\dist (bit_extender_1_out), .out(sll));
  Shifter #(.width(16), .shift("lr")) shifter_2 (.in(X), .\dist (bit_extender_2_out), .out(srl));
  Multiplexer #(.select(3), .width(16)) multiplexer_2 (
    .in0(sll), .in1(srl), .in2(add), .in3(\and ), .in4(\or ), .in5(\xor ), .in6(slt), .in7(out_8),
    .out(Result_2), .sel(Switch));  // open: en

  // Other names for the same wires on the sheet: lower[15:0] = out_7; S[2:0] = Switch; upper[15:0] = out_8

  // Notes on the sheet:
  //   INPUTS to your circuit
  //   DON'T CHANGE THE LOCATIONS OF THE INPUTS AND OUTPUTS!
  //   OUTPUTS from your circuit
endmodule
