// Logisim project cpu.circ as structural Verilog: 2 circuits, main circuit main
module main (
  input  [15:0] INSTRUCTION,
  input  CLOCK,
  output [15:0] FETCH_ADDRESS,
  output [15:0] s0_Value,
  output [15:0] s1_Value,
  output [15:0] s2_Value,
  output [15:0] ra_Value,
  output [15:0] sp_Value,
  output [15:0] HI_Value,
  output [15:0] LO_Value
);

  wire ALUsrc, bne, branch, branch_check, comparator_1_eq, comparator_2_eq, comparator_3_eq, comparator_4_eq,
       comparator_5_eq, comparator_6_eq, Ext_Op, j_and_jr, Jump, main_2_equal, MemToReg, MemWri,
       multiplexer_7_out, multiply, not_1_out, or_1_out, or_2_out, RegDst, RegWri, U;
  wire [1:0] adder_4_out, adder_5_out, bit_extender_5_out, bit_extender_6_out, bit_extender_7_out,
       bit_extender_8_out, check, shifter_3_out, shifter_4_out;
  wire [2:0] ALUctr, extend_rd, multiplexer_2_out, multiplexer_3_out;
  wire [9:0] extend_immediate;
  wire [15:0] adder_2_out, adder_3_out, and_1_out, bit_extender_1_out, bit_extender_2_out,
       bit_extender_3_out, bit_extender_4_out, jump_addr, main_1_read_data_1, main_1_read_data_2,
       main_2_result, main_2_result_2, MEM_p5, multiplexer_1_out, multiplexer_5_out, multiplexer_6_out,
       multiplexer_8_out, multiplexer_9_out, multiplexer_10_out, multiplexer_11_out, pc_imm, shifter_1_out,
       shifter_2_out;
  wire [15:10] instr_bubble;

  Adder #(.width(16)) adder_1 (.a(and_1_out), .b(bit_extender_1_out), .out(jump_addr));  // open: cin, cout
  Multiplexer #(.width(16), .enable("false")) multiplexer_1 (
    .in0(multiplexer_5_out), .in1(jump_addr), .out(multiplexer_1_out), .sel(Jump));
  assign and_1_out = 16'hfc00 & adder_2_out;  // AND_Gate and_1, 16 bits wide
  assign bit_extender_1_out = {{6{1'b0}}, extend_immediate};  // Bit_Extender bit_extender_1
  Register #(.width(16)) PC (.D(multiplexer_1_out), .Q(FETCH_ADDRESS), .clk(CLOCK));  // open: en, clr
  Adder #(.width(16)) adder_2 (.a(FETCH_ADDRESS), .b(16'h2), .out(adder_2_out));  // open: cin, cout
  Shifter #(.width(16)) shifter_1 (.in(pc_imm), .\dist (4'b0001), .out(shifter_1_out));
  or or_1 (or_1_out, MemWri, branch);
  assign bit_extender_2_out = {{10{1'b0}}, extend_immediate[5:0]};  // Bit_Extender bit_extender_2
  assign bit_extender_3_out = {{10{extend_immediate[5]}}, extend_immediate[5:0]};  // Bit_Extender bit_extender_3
  Adder #(.width(16)) adder_3 (.a(shifter_1_out), .b(adder_2_out), .out(adder_3_out));  // open: cin, cout
  Multiplexer #(.width(3), .enable("false")) multiplexer_2 (
    .in0(extend_immediate[5:3]), .in1({instr_bubble[11:10], extend_immediate[9]}), .out(multiplexer_2_out),
    .sel(or_1_out));
  Multiplexer #(.width(3), .enable("false")) multiplexer_3 (
    .in0({instr_bubble[11:10], extend_immediate[9]}), .in1(extend_rd), .out(multiplexer_3_out), .sel(U));
  Multiplexer #(.width(16), .enable("false")) multiplexer_4 (
    .in0(bit_extender_2_out), .in1(bit_extender_3_out), .out(pc_imm), .sel(Ext_Op));
  or or_2 (or_2_out, branch_check, j_and_jr);
  Multiplexer #(.width(16), .enable("false")) multiplexer_5 (
    .in0(adder_2_out), .in1(adder_3_out), .out(multiplexer_5_out), .sel(branch_check));
  and and_2 (branch_check, multiplexer_7_out, branch);
  Multiplexer #(.width(16), .enable("false")) multiplexer_6 (
    .in0(INSTRUCTION), .in1({16{1'b0}}), .out(multiplexer_6_out), .sel(or_2_out));
  Register #(.width(16)) instr_reg (
    .D(multiplexer_6_out), .Q({instr_bubble, extend_immediate}), .clk(CLOCK));  // open: en, clr
  regfile_main main_1 (
    .Read_Register_1(extend_immediate[8:6]), .Read_Register_2(multiplexer_2_out),
    .Write_Register(multiplexer_3_out), .Write_Data(multiplexer_9_out), .Write_Enable(RegWri), .Clock(CLOCK),
    .Read_Data_1(main_1_read_data_1), .Read_Data_2(main_1_read_data_2), .s0_Value(s0_Value),
    .s1_Value(s1_Value), .s2_Value(s2_Value), .ra_Value(ra_Value), .sp_Value(sp_Value));
  Multiplexer #(.enable("false")) multiplexer_7 (
    .in0(main_2_equal), .in1(not_1_out), .out(multiplexer_7_out), .sel(bne));
  not not_1 (not_1_out, main_2_equal);
  alu_main main_2 (
    .Switch(ALUctr), .X(main_1_read_data_1), .Equal(main_2_equal), .Result(main_2_result),
    .Y(multiplexer_8_out), .Result_2(main_2_result_2));  // open: out_7, out_8
  Multiplexer #(.width(16), .enable("false")) multiplexer_8 (
    .in0(main_1_read_data_2), .in1(pc_imm), .out(multiplexer_8_out), .sel(ALUsrc));
  Multiplexer #(.select(2), .width(16), .enable("false")) multiplexer_9 (
    .in0(multiplexer_10_out), .in1(LO_Value), .in2(HI_Value), .in3(FETCH_ADDRESS), .out(multiplexer_9_out),
    .sel(check));
  Register #(.width(16)) HI (.D(main_2_result_2), .en(multiply), .Q(HI_Value), .clk(CLOCK));  // open: clr
  assign bit_extender_4_out = {{6{1'b0}}, extend_immediate};  // Bit_Extender bit_extender_4
  Comparator #(.width(4), .mode("unsigned")) comparator_1 (
    .a(instr_bubble[15:12]), .b(4'b0001), .eq(comparator_1_eq));  // open: gt, lt
  assign bit_extender_5_out = {{1{1'b0}}, multiply};  // Bit_Extender bit_extender_5
  // mem_main MEM: pin names not known; wires that end beside it: main_2_result, main_1_read_data_2, MemWri, CLOCK, MEM_p5
  Shifter #(.width(16)) shifter_2 (.in(bit_extender_4_out), .\dist (4'b0110), .out(shifter_2_out));
  assign bit_extender_6_out = {{1{1'b0}}, comparator_1_eq};  // Bit_Extender bit_extender_6
  Shifter #(.width(2)) shifter_3 (.in(bit_extender_5_out), .\dist (1'b1), .out(shifter_3_out));
  Multiplexer #(.width(16), .enable("false")) multiplexer_10 (
    .in0(main_2_result), .in1(MEM_p5), .out(multiplexer_10_out), .sel(MemToReg));
  Multiplexer #(.select(2), .width(16), .enable("false")) multiplexer_11 (
    .in0(LO_Value), .in1(shifter_2_out), .in2(main_2_result), .out(multiplexer_11_out), .sel(adder_4_out));  // open: in3
  Adder #(.width(2)) adder_4 (.a(bit_extender_6_out), .b(shifter_3_out), .out(adder_4_out));  // open: cin, cout
  Register #(.width(16)) LO (.D(multiplexer_11_out), .Q(LO_Value), .clk(CLOCK));  // open: en, clr
  Comparator #(.width(4), .mode("unsigned")) comparator_2 (
    .a(instr_bubble[15:12]), .b(4'b1100), .eq(comparator_2_eq));  // open: gt, lt
  ControlUnit controlunit_1 (
    .opcode(instr_bubble[15:12]), .funct(extend_immediate[2:0]), .jump(Jump), .ExtOp(Ext_Op),
    .branch(branch), .ALUSrc(ALUsrc), .ALUCtr(ALUctr), .MemWR(MemWri), .MemtoReg(MemToReg), .RegWR(RegWri),
    .RegDst(RegDst), .U(U), .bne(bne));  // open: R, I
  Comparator #(.width(4), .mode("unsigned")) comparator_3 (
    .a(instr_bubble[15:12]), .b(4'b1101), .eq(comparator_3_eq));  // open: gt, lt
  assign bit_extender_7_out = {{1{1'b0}}, comparator_2_eq};  // Bit_Extender bit_extender_7
  Comparator #(.width(4), .mode("unsigned")) comparator_4 (
    .a(instr_bubble[15:12]), .b(4'b0010), .eq(comparator_4_eq));  // open: gt, lt
  Comparator #(.width(4), .mode("unsigned")) comparator_5 (
    .a(instr_bubble[15:12]), .b(4'b0011), .eq(comparator_5_eq));  // open: gt, lt
  Comparator #(.width(3), .mode("unsigned")) comparator_6 (
    .a(extend_immediate[2:0]), .b(3'b111), .eq(comparator_6_eq));  // open: gt, lt
  assign bit_extender_8_out = {{1{1'b0}}, comparator_3_eq};  // Bit_Extender bit_extender_8
  Shifter #(.width(2)) shifter_4 (.in(bit_extender_7_out), .\dist (1'b1), .out(shifter_4_out));
  or or_3 (j_and_jr, comparator_4_eq, comparator_5_eq);
  and and_3 (multiply, RegDst, comparator_6_eq);
  Adder #(.width(2)) adder_5 (.a(bit_extender_8_out), .b(shifter_4_out), .out(adder_5_out));  // open: cin, cout
  assign extend_rd = {{1{1'b0}}, instr_bubble[11:10]};  // Bit_Extender bit_extender_9
  Multiplexer #(.width(2), .enable("false")) multiplexer_12 (
    .in0(adder_5_out), .in1(2'b11), .out(check), .sel(j_and_jr));

  // Other names for the same wires on the sheet: clk = CLOCK; fetch_addr[15:0] = FETCH_ADDRESS; HI[15:0] = HI_Value;
  //   funct[2:0] = extend_immediate[2:0]; immediate[5:0] = extend_immediate[5:0];
  //   instr_bubble[9:0] = extend_immediate; rt[2:0] = extend_immediate[5:3]; rs[2:0] = extend_immediate[8:6];
  //   rd[2:0] = {instr_bubble[11:10], extend_immediate[9]}; opcode[3:0] = instr_bubble[15:12]; LO[15:0] = LO_Value;
  //   ra[15:0] = ra_Value; s0[15:0] = s0_Value; s1[15:0] = s1_Value; s2[15:0] = s2_Value; sp[15:0] = sp_Value

  // Notes on the sheet:
  //   Output
  //   These are outputs/inputs from run.circ
  //   Inputs
  //   These are DEBUG/TEST outputs from your circuit.
  //   Check bubble or instr
  //   Controller Module
  //   J & JR
  //   Check Multiply
  //   Decode Module
  //   Check
endmodule

module ControlUnit (
  input  [3:0] opcode,
  input  [2:0] funct,
  output jump,
  output ExtOp,
  output branch,
  output ALUSrc,
  output [2:0] ALUCtr,
  output MemWR,
  output MemtoReg,
  output RegWR,
  output RegDst,
  output R,
  output U,
  output I,
  output bne
);

  wire and_1_out, comparator_7_eq, comparator_9_eq, comparator_12_eq, comparator_13_eq, comparator_14_eq,
       comparator_15_eq, comparator_16_eq, comparator_17_eq, comparator_18_eq, comparator_19_eq,
       comparator_20_eq, comparator_21_eq, comparator_22_eq, comparator_23_eq, comparator_24_eq,
       comparator_25_eq, comparator_26_eq, comparator_27_eq, comparator_28_eq, j, lui, not_2_out;
  wire [2:0] multiplexer_1_out;

  Comparator #(.width(4), .mode("unsigned")) comparator_1 (.a(opcode), .b(4'b0000), .eq(R));  // open: gt, lt
  Comparator #(.width(4), .mode("unsigned")) comparator_2 (.a(opcode), .b(4'b0001), .eq(lui));  // open: gt, lt
  Comparator #(.width(4), .mode("unsigned")) comparator_3 (.a(opcode), .b(4'b0010), .eq(j));  // open: gt, lt
  Comparator #(.width(4), .mode("unsigned")) comparator_4 (.a(opcode), .b(4'b0010), .gt(I));  // open: eq, lt
  or or_1 (U, lui, j);
  Comparator #(.width(4), .mode("unsigned")) comparator_5 (.a(opcode), .b(4'b0010), .eq(jump));  // open: gt, lt
  Comparator #(.width(4), .mode("unsigned")) comparator_6 (.a(opcode), .b(4'b0000), .eq(RegDst));  // open: gt, lt
  Comparator #(.width(4), .mode("unsigned")) comparator_7 (
    .a(opcode), .b(4'b0100), .eq(comparator_7_eq));  // open: gt, lt
  Comparator #(.width(4), .mode("unsigned")) comparator_8 (.a(opcode), .b(4'b1011), .eq(MemWR));  // open: gt, lt
  not not_1 (ALUSrc, comparator_9_eq);
  Comparator #(.width(4), .mode("unsigned")) comparator_9 (
    .a(opcode), .b(4'b0000), .eq(comparator_9_eq));  // open: gt, lt
  Comparator #(.width(4), .mode("unsigned")) comparator_10 (.a(opcode), .b(4'b1010), .eq(MemtoReg));  // open: gt, lt
  or or_2 (branch, comparator_7_eq, bne);
  Comparator #(.width(4), .mode("unsigned")) comparator_11 (.a(opcode), .b(4'b0101), .eq(bne));  // open: gt, lt
  Multiplexer #(.select(4), .width(3), .enable("false")) multiplexer_1 (
    .in1(3'b000), .in3(3'b010), .in4(3'b010), .in5(3'b010), .in6(3'b010), .in7(3'b110), .in8(3'b011),
    .in9(3'b100), .in10(3'b010), .in11(3'b010), .out(multiplexer_1_out), .sel(opcode));  // open: in0, in2, in12, in13, in14, in15
  Comparator #(.width(4), .mode("unsigned")) comparator_12 (
    .a(opcode), .b(4'b0011), .eq(comparator_12_eq));  // open: gt, lt
  Comparator #(.width(4), .mode("unsigned")) comparator_13 (
    .a(opcode), .b(4'b0100), .eq(comparator_13_eq));  // open: gt, lt
  Comparator #(.width(4), .mode("unsigned")) comparator_14 (
    .a(opcode), .b(4'b0101), .eq(comparator_14_eq));  // open: gt, lt
  Comparator #(.width(4), .mode("unsigned")) comparator_15 (
    .a(opcode), .b(4'b0110), .eq(comparator_15_eq));  // open: gt, lt
  Comparator #(.width(4), .mode("unsigned")) comparator_16 (
    .a(opcode), .b(4'b0111), .eq(comparator_16_eq));  // open: gt, lt
  Comparator #(.width(4), .mode("unsigned")) comparator_17 (
    .a(opcode), .b(4'b1010), .eq(comparator_17_eq));  // open: gt, lt
  Comparator #(.width(4), .mode("unsigned")) comparator_18 (
    .a(opcode), .b(4'b1011), .eq(comparator_18_eq));  // open: gt, lt
  Multiplexer #(.width(3), .enable("false")) multiplexer_2 (
    .in0(multiplexer_1_out), .in1(funct), .out(ALUCtr), .sel(R));
  or or_3 (ExtOp, comparator_12_eq, comparator_13_eq, comparator_14_eq, comparator_15_eq, comparator_16_eq, comparator_17_eq, comparator_18_eq);
  Comparator #(.width(3)) comparator_19 (.a(funct), .b(3'b111), .eq(comparator_19_eq));  // open: gt, lt
  not not_2 (not_2_out, comparator_19_eq);
  and and_1 (and_1_out, not_2_out, R);
  Comparator #(.width(4), .mode("unsigned")) comparator_20 (
    .a(opcode), .b(4'b0110), .eq(comparator_20_eq));  // open: gt, lt
  Comparator #(.width(4), .mode("unsigned")) comparator_21 (
    .a(opcode), .b(4'b0111), .eq(comparator_21_eq));  // open: gt, lt
  Comparator #(.width(4), .mode("unsigned")) comparator_22 (
    .a(opcode), .b(4'b1000), .eq(comparator_22_eq));  // open: gt, lt
  Comparator #(.width(4), .mode("unsigned")) comparator_23 (
    .a(opcode), .b(4'b1001), .eq(comparator_23_eq));  // open: gt, lt
  Comparator #(.width(4), .mode("unsigned")) comparator_24 (
    .a(opcode), .b(4'b1010), .eq(comparator_24_eq));  // open: gt, lt
  Comparator #(.width(4), .mode("unsigned")) comparator_25 (
    .a(opcode), .b(4'b1100), .eq(comparator_25_eq));  // open: gt, lt
  Comparator #(.width(4), .mode("unsigned")) comparator_26 (
    .a(opcode), .b(4'b1101), .eq(comparator_26_eq));  // open: gt, lt
  Comparator #(.width(4), .mode("unsigned")) comparator_27 (
    .a(opcode), .b(4'b0010), .eq(comparator_27_eq));  // open: gt, lt
  Comparator #(.width(4), .mode("unsigned")) comparator_28 (
    .a(opcode), .b(4'b0011), .eq(comparator_28_eq));  // open: gt, lt
  or or_4 (RegWR, and_1_out, comparator_20_eq, comparator_21_eq, comparator_22_eq, comparator_23_eq, comparator_24_eq, comparator_25_eq, comparator_26_eq, comparator_27_eq, comparator_28_eq);

  // Other names for the same wires on the sheet: MemReg = MemtoReg

  // Notes on the sheet:
  //   Input of Controller
  //   Select instruction type
  //   Control output
  //   Jump
  //   RegDst
  //   Branch
  //   MemWR
  //   ALUSrc
  //   MemtoReg
  //   bne
  //   ExtOp
  //   ALUCtr
  //   RegWR
endmodule
